# Fritzing sketch connections (saved by Fritzing 0.9.9b)
breadboards: 1

parts:
  R1 = Rotary Potentiometer (Small) [maximum_resistance=100kΩ package=THT]
  R2 = Resistor [tolerance=±5% resistance=220 package=THT]
  S1 = Pushbutton [package="[THT]"]
  Part1 = Arduino Nano (Rev3.0)
  OLED1 = OLED 128x64 I2C Monochrome Display

nets:
  N1: R1.wiper, Part1.A0
  N2: R1.leg2, S1.Pin_1, S1.Pin_2
  N3: R2.Pin_0, S1.Pin_3, S1.Pin_4, Part1.D2
  N4: R2.Pin_1, OLED1.GND
  N5: Part1.A5, OLED1.SCK
  N6: Part1.A4, OLED1.SDA
